// Logisim project BCDtoDECdecoder.circ as structural Verilog: 3 circuits, main circuit main
module main (
);

  wire basiccounter_1_c1, basiccounter_1_c2, basiccounter_1_c3, basiccounter_1_c4, bcdtodec_1_d0,
       bcdtodec_1_d1, bcdtodec_1_d2, bcdtodec_1_d3, bcdtodec_1_d4, bcdtodec_1_d5, bcdtodec_1_d6,
       bcdtodec_1_d7, bcdtodec_1_d8, bcdtodec_1_d9, button_1_out, clock_1_out;

  Clock clock_1 (.out(clock_1_out));
  Button button_1 (.out(button_1_out));
  BasicCounter basiccounter_1 (
    .clk(clock_1_out), .R(button_1_out), .C4(basiccounter_1_c4), .C3(basiccounter_1_c3),
    .C2(basiccounter_1_c2), .C1(basiccounter_1_c1));
  BCDtoDEC bcdtodec_1 (
    .A3(basiccounter_1_c4), .A2(basiccounter_1_c3), .A1(basiccounter_1_c2), .A0(basiccounter_1_c1),
    .D9(bcdtodec_1_d9), .D8(bcdtodec_1_d8), .D7(bcdtodec_1_d7), .D6(bcdtodec_1_d6), .D5(bcdtodec_1_d5),
    .D4(bcdtodec_1_d4), .D3(bcdtodec_1_d3), .D2(bcdtodec_1_d2), .D1(bcdtodec_1_d1), .D0(bcdtodec_1_d0));
  LED led_1 (.in(bcdtodec_1_d9));
  LED led_2 (.in(bcdtodec_1_d8));
  LED led_3 (.in(bcdtodec_1_d7));
  LED led_4 (.in(bcdtodec_1_d6));
  LED led_5 (.in(bcdtodec_1_d5));
  LED led_6 (.in(bcdtodec_1_d4));
  LED led_7 (.in(bcdtodec_1_d3));
  LED led_8 (.in(bcdtodec_1_d2));
  LED led_9 (.in(bcdtodec_1_d1));
  LED led_10 (.in(bcdtodec_1_d0));

  // Notes on the sheet:
  //   BCD to Decimal Decoder
endmodule

module BCDtoDEC (
  input  A3,
  input  A2,
  input  A1,
  input  A0,
  output D9,
  output D8,
  output D7,
  output D6,
  output D5,
  output D4,
  output D3,
  output D2,
  output D1,
  output D0
);

  wire not_1_out, not_2_out, not_3_out, not_4_out, not_5_out, not_6_out, not_7_out, not_8_out, not_9_out,
       not_10_out, not_11_out, not_12_out, not_13_out, not_14_out, not_15_out;

  and and_1 (D9, A3, A0);
  and and_2 (D8, A3, not_1_out);
  not not_1 (not_1_out, A0);
  and and_3 (D7, A2, A1, A0);
  and and_4 (D6, A2, A1, not_2_out);
  not not_2 (not_2_out, A0);
  not not_3 (not_3_out, A1);
  and and_5 (D5, A2, not_3_out, A0);
  not not_4 (not_4_out, A1);
  and and_6 (D4, A2, not_4_out, not_5_out);
  not not_5 (not_5_out, A0);
  not not_6 (not_6_out, A2);
  and and_7 (D3, not_6_out, A1, A0);
  not not_7 (not_7_out, A2);
  and and_8 (D2, not_7_out, A1, not_8_out);
  not not_8 (not_8_out, A0);
  not not_9 (not_9_out, A3);
  not not_10 (not_10_out, A2);
  not not_11 (not_11_out, A1);
  not not_12 (not_12_out, A3);
  not not_13 (not_13_out, A2);
  not not_14 (not_14_out, A1);
  not not_15 (not_15_out, A0);
  and and_9 (D1, not_9_out, not_10_out, not_11_out, A0);
  and and_10 (D0, not_12_out, not_13_out, not_14_out, not_15_out);
endmodule

module BasicCounter (
  input  clk,
  input  R,
  output C4,
  output C3,
  output C2,
  output C1
);

  wire d_ff_1_qn, d_ff_2_qn, d_ff_3_qn, d_ff_4_qn;

  D_Flip_Flop d_ff_1 (.D(d_ff_1_qn), .clk(clk), .Q(C1), .Qn(d_ff_1_qn), .reset(R));  // open: preset
  D_Flip_Flop d_ff_2 (.D(d_ff_2_qn), .clk(d_ff_1_qn), .Q(C2), .Qn(d_ff_2_qn), .reset(R));  // open: preset
  D_Flip_Flop d_ff_3 (.D(d_ff_3_qn), .clk(d_ff_2_qn), .Q(C3), .Qn(d_ff_3_qn), .reset(R));  // open: preset
  D_Flip_Flop d_ff_4 (.D(d_ff_4_qn), .clk(d_ff_3_qn), .Q(C4), .Qn(d_ff_4_qn), .reset(R));  // open: preset
endmodule
